# Fritzing sketch _04_analogRead (saved by Fritzing 0.9.3b)
breadboards: 1

parts:
  부품1 = orange board (Rev3)
  R1 = Rotary Potentiometer (Small) [maximum_resistance=100kΩ package=THT]

nets:
  N1: 부품1.A0, R1.wiper
  N2: 부품1.5V, R1.leg1
  N3: 부품1.GND, R1.leg2

custom parts:
  orange board (Rev3): The orange board is a microcontroller board based on the ATmega328 (datasheet). It has 14 digital input/output pins (of which 6 can be used as PWM outputs), 6 analog inputs, a 16 MHz ceramic resonator, a USB connection, a power jack, an ICSP header, and a reset button. It contains everything needed to support the microcontroller; simply connect it to a computer with a USB cable or power it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
