# Fritzing sketch _05_analogWrite (saved by Fritzing 0.9.3b)
breadboards: 1

parts:
  부품1 = orange board (Rev3)
  R1 = Resistor [tolerance=±5% resistance=220 package=THT]
  LED1 = LED - 5mm [color="Red (633nm)" package="5 mm [THT]"]
  R2 = Photocell (LDR) [package=THT]
  R3 = Resistor [tolerance=±5% resistance=10k package=THT]

nets:
  N1: 부품1.A0, R2.pin_1, R3.Pin_1
  N2: 부품1.D11_PWM/MOSI, LED1.anode
  N3: 부품1.5V, R2.pin_0
  N4: 부품1.GND, R1.Pin_0, R3.Pin_0
  N5: R1.Pin_1, LED1.cathode

custom parts:
  orange board (Rev3): The orange board is a microcontroller board based on the ATmega328 (datasheet). It has 14 digital input/output pins (of which 6 can be used as PWM outputs), 6 analog inputs, a 16 MHz ceramic resonator, a USB connection, a power jack, an ICSP header, and a reset button. It contains everything needed to support the microcontroller; simply connect it to a computer with a USB cable or power it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
