# Fritzing sketch Untitled Sketch (saved by Fritzing 0.9.0b)
breadboards: 1

parts:
  부품1 = Arduino Uno (Rev3)
  부품2 = Bluetooth HM-10

nets:
  N1: 부품1.D2, 부품2.TXD
  N2: 부품1.D4, 부품2.RXD
  5V: 부품1.5V, 부품2.VCC
  GND: 부품1.GND, 부품2.GND
