# Fritzing sketch minicar_02_ultra_1 (saved by Fritzing 0.9.3b)
breadboards: 1

parts:
  부품1 = Arduino Nano (Rev3.0)
  hc-sr1 = hc-sr04

nets:
  GND: 부품1.GND, hc-sr1.GND
  N1: 부품1.D5, hc-sr1.Trig
  N2: 부품1.D6, hc-sr1.Echo
  5V: 부품1.5V, hc-sr1.VCC
