# Fritzing sketch minicar_03_motor_1 (saved by Fritzing 0.9.3b)
breadboards: 1

parts:
  부품1 = Arduino Nano (Rev3.0)
  Q1 = NPN-Transistor [package="TO92 [THT]"]
  R1 = Resistor [tolerance=±5% resistance=220 package=THT]
  M1 = DC Motor

nets:
  N1: 부품1.GND, M1.pin_2
  N2: 부품1.D9, R1.Pin_1
  N3: 부품1.5V, Q1.C
  N4: Q1.E, M1.pin_1
  N5: Q1.B, R1.Pin_0
