# Fritzing sketch minicar_05_2motorandultra_1 (saved by Fritzing 0.9.3b)
breadboards: 1

parts:
  부품1 = Arduino Nano (Rev3.0)
  Q1 = NPN-Transistor [package="TO92 [THT]"]
  R1 = Resistor [tolerance=±5% resistance=220 package=THT]
  Q2 = NPN-Transistor [package="TO92 [THT]"]
  R2 = Resistor [tolerance=±5% resistance=220 package=THT]
  M1 = DC Motor
  M2 = DC Motor
  hc-sr1 = hc-sr04

nets:
  GND: 부품1.GND, M1.pin_1, M2.pin_1, hc-sr1.GND
  N1: 부품1.D5, hc-sr1.Echo
  N2: 부품1.D6, hc-sr1.Trig
  N3: 부품1.D9, R1.Pin_1
  N4: 부품1.D10, R2.Pin_1
  VIN: 부품1.VIN, Q1.C, Q2.C, hc-sr1.VCC
  N5: Q1.E, M1.pin_2
  N6: Q1.B, R1.Pin_0
  N7: Q2.E, M2.pin_2
  N8: Q2.B, R2.Pin_0
