# Fritzing sketch mkr1000_ili9341_dht11 (saved by Fritzing 0.9.3b)
breadboards: 1

parts:
  부품1 = TFT 2.2 inch 320x240 w microSD [part_number=1480]
  부품2 = Arduino MKR1000
  DHT1 = DHT11 Humitidy and Temperature Sensor
  R1 = Resistor [tolerance=±5% resistance=10k package=THT]

nets:
  GND: 부품1.GND, 부품2.GND, DHT1.GND
  VIN: 부품1.VIN, 부품1.BACKLIGHT, 부품2.VCC
  N1: 부품1.DC, 부품2.D7
  N2: 부품1.RESET, 부품2.D5_PWM
  N3: 부품1.SDCS, 부품2.D10_MISO
  N4: 부품1.LCDCS, 부품2.D6
  N5: 부품1.MOSI, 부품2.D8_MOSI
  N6: 부품1.SCLK, 부품2.D9_SCK
  N7: 부품2.D2_PWM, DHT1.DATA, R1.Pin_1
  5V: 부품2.D4_PWM, 부품2.5V, DHT1.VDD, R1.Pin_0

custom parts:
  TFT 2.2 inch 320x240 w microSD: This lovely little display breakout is the best way to add a small, colorful and bright display to any project. Since the display uses 4-wire SPI to communicate and has its own pixel-addressable frame buffer, it can be used with every kind of microcontroller. Even a very small one with low memory and few pins available! The 2.2" display has 320x240 color pixels.
  Arduino MKR1000: MKR1000 is a powerful board that combines the functionality of the Zero and the Wi-Fi Shield. It is the ideal solution for makers wanting to design IoT projects with minimal previous experience in networking
  DHT11 Humitidy and Temperature Sensor: DHT11 Humidity and Temperature Sensor
