# Fritzing sketch moon_light (saved by Fritzing 0.9.3b)
perfboards: 1

parts:
  부품1 = Arduino Nano (Rev3.0)
  U1 = SWITCH_SPDT [package=kps-1290]
  부품2 = 16 NeoPixel Ring [part_number=1463]
  R1 = Rotary Potentiometer (Small) [maximum_resistance=100kΩ package=THT]
  S1 = Pushbutton [package="[THT]"]

nets:
  GND: 부품1.GND, 부품2.GND, R1.leg2, S1.Pin_3, S1.Pin_4
  N1: 부품1.D3, S1.Pin_1, S1.Pin_2
  N2: 부품1.D5, 부품2.IN
  N3: 부품1.5V, U1.P
  N4: 부품1.A0, R1.wiper
  N5: U1.S, 부품2.VDD, R1.leg1

custom parts:
  16 NeoPixel Ring: 16 ultra bright smart LED NeoPixels are arranged in a circle with 1.75" (44.5mm) outer diameter. The rings are 'chainable' - connect the output pin of one to the input pin of another. Use only one microcontroller pin to control as many as you can chain together! Each LED is addressable as the driver chip is inside the LED. Each one has ~18mA constant current drive so the color will be very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
