# Fritzing sketch 160625_hangul_clock (saved by Fritzing 0.9.3b)
perfboards: 1

parts:
  LED1 = Super Flux LED blue [color=Blue]
  LED2 = Super Flux LED blue [color=Blue]
  LED3 = Super Flux LED blue [color=Blue]  # not connected
  LED4 = Super Flux LED blue [color=Blue]  # not connected
  LED5 = Super Flux LED blue [color=Blue]  # not connected
  LED6 = Super Flux LED blue [color=Blue]  # not connected
  LED7 = Super Flux LED blue [color=Blue]  # not connected
  LED8 = Super Flux LED blue [color=Blue]  # not connected
  LED9 = Super Flux LED blue [color=Blue]  # not connected
  LED10 = Super Flux LED blue [color=Blue]  # not connected
  LED11 = Super Flux LED blue [color=Blue]  # not connected
  LED12 = Super Flux LED blue [color=Blue]  # not connected
  LED13 = Super Flux LED blue [color=Blue]  # not connected
  LED14 = Super Flux LED blue [color=Blue]  # not connected
  LED15 = Super Flux LED blue [color=Blue]  # not connected
  LED16 = Super Flux LED blue [color=Blue]  # not connected
  LED17 = Super Flux LED blue [color=Blue]  # not connected
  LED18 = Super Flux LED blue [color=Blue]  # not connected
  LED19 = Super Flux LED blue [color=Blue]  # not connected
  LED20 = Super Flux LED blue [color=Blue]  # not connected
  LED21 = Super Flux LED blue [color=Blue]  # not connected
  LED22 = Super Flux LED blue [color=Blue]  # not connected
  LED23 = Super Flux LED blue [color=Blue]  # not connected
  LED24 = Super Flux LED blue [color=Blue]  # not connected
  LED25 = Super Flux LED blue [color=Blue]  # not connected

nets:
  N1: LED1.cathode, LED2.anode
