# Fritzing sketch 160627_hangul_clock (saved by Fritzing 0.9.3b)
perfboards: 1

parts:
  LED1 = Super Flux LED blue [color=Blue]
  LED2 = Super Flux LED blue [color=Blue]  # not connected
  LED3 = Super Flux LED blue [color=Blue]  # not connected
  LED4 = Super Flux LED blue [color=Blue]  # not connected
  LED5 = Super Flux LED blue [color=Blue]  # not connected
  LED6 = Super Flux LED blue [color=Blue]
  LED7 = Super Flux LED blue [color=Blue]  # not connected
  LED8 = Super Flux LED blue [color=Blue]  # not connected
  LED9 = Super Flux LED blue [color=Blue]  # not connected
  LED10 = Super Flux LED blue [color=Blue]  # not connected
  LED11 = Super Flux LED blue [color=Blue]
  LED12 = Super Flux LED blue [color=Blue]  # not connected
  LED13 = Super Flux LED blue [color=Blue]  # not connected
  LED14 = Super Flux LED blue [color=Blue]  # not connected
  LED15 = Super Flux LED blue [color=Blue]  # not connected
  LED16 = Super Flux LED blue [color=Blue]
  LED17 = Super Flux LED blue [color=Blue]
  LED18 = Super Flux LED blue [color=Blue]  # not connected
  LED19 = Super Flux LED blue [color=Blue]
  LED20 = Super Flux LED blue [color=Blue]  # not connected
  LED21 = Super Flux LED blue [color=Blue]  # not connected
  LED22 = Super Flux LED blue [color=Blue]  # not connected
  LED23 = Super Flux LED blue [color=Blue]  # not connected
  LED24 = Super Flux LED blue [color=Blue]
  LED25 = Super Flux LED blue [color=Blue]
  S1 = Pushbutton [package="[THT]"]
  S2 = Pushbutton [package="[THT]"]
  R1 = Resistor [tolerance=±5% resistance=10k package=THT]
  R2 = Resistor [tolerance=±5% resistance=10k package=THT]

nets:
  N1: LED1.anode, LED6.anode
  N2: LED11.anode, LED16.anode
  N3: LED17.cathode, LED19.anode
  N4: LED24.cathode, LED25.cathode
  N5: S1.Pin_1, S1.Pin_2, R1.Pin_0
  N6: S1.Pin_3, S1.Pin_4
  N7: S2.Pin_1, S2.Pin_2, R2.Pin_0
  N8: S2.Pin_3, S2.Pin_4
