# Fritzing sketch 160721_hangul_clock_pcb (saved by Fritzing 0.9.3b)
perfboards: 2

parts:
  LED1 = Super Flux LED blue [color=Blue]
  LED2 = Super Flux LED blue [color=Blue]
  LED3 = Super Flux LED blue [color=Blue]
  LED4 = Super Flux LED blue [color=Blue]
  LED5 = Super Flux LED blue [color=Blue]
  LED6 = Super Flux LED blue [color=Blue]
  LED7 = Super Flux LED blue [color=Blue]
  LED8 = Super Flux LED blue [color=Blue]
  LED9 = Super Flux LED blue [color=Blue]
  LED10 = Super Flux LED blue [color=Blue]
  LED12 = Super Flux LED blue [color=Blue]
  LED13 = Super Flux LED blue [color=Blue]
  LED14 = Super Flux LED blue [color=Blue]  # not connected
  LED15 = Super Flux LED blue [color=Blue]  # not connected
  LED16 = Super Flux LED blue [color=Blue]  # not connected
  LED17 = Super Flux LED blue [color=Blue]  # not connected
  LED18 = Super Flux LED blue [color=Blue]  # not connected
  LED19 = Super Flux LED blue [color=Blue]  # not connected
  LED20 = Super Flux LED blue [color=Blue]  # not connected
  LED21 = Super Flux LED blue [color=Blue]  # not connected
  LED22 = Super Flux LED blue [color=Blue]  # not connected
  LED23 = Super Flux LED blue [color=Blue]  # not connected
  LED24 = Super Flux LED blue [color=Blue]  # not connected
  LED25 = Super Flux LED blue [color=Blue]  # not connected
  LED26 = Super Flux LED blue [color=Blue]  # not connected
  J1 = female pin header, 15 pins [form="♀ (female)"]
  J2 = female pin header, 15 pins [form="♀ (female)"]
  S1 = Pushbutton [package="[THT]"]
  S2 = Pushbutton [package="[THT]"]
  R1 = Resistor [tolerance=±5% resistance=10k package=THT]
  R2 = Resistor [tolerance=±5% resistance=10k package=THT]
  J6 = female pin header, 6 pins [form="♀ (female)"]

nets:
  N1: LED1.anode, J1.pin15
  N2: LED1.cathode, LED2.anode
  N3: LED2.cathode, LED3.anode
  N4: LED3.cathode, LED4.anode
  N5: LED4.cathode, LED5.anode
  N6: LED5.cathode, LED6.anode
  N7: LED6.cathode, LED7.anode
  N8: LED7.cathode, LED8.anode
  N9: LED8.cathode, LED9.anode
  N10: LED9.cathode, LED10.anode
  N11: LED10.cathode, LED13.anode
  N12: LED12.anode, LED13.cathode
  N13: J1.pin13, J1.pin14, J2.pin5, S1.Pin_3, S1.Pin_4, S2.Pin_3, S2.Pin_4, R1.Pin_1, R2.Pin_1, J6.pin2
  N14: J2.pin3, R1.Pin_0, R2.Pin_0, J6.pin1
  N15: J2.pin7, J6.pin4
  N16: J2.pin8, J6.pin3
  N17: S1.Pin_1, S1.Pin_2
  N18: S2.Pin_1, S2.Pin_2
