# Fritzing sketch 160726_hangul_clock (saved by Fritzing 0.9.3b)
perfboards: 2

parts:
  LED1 = Super Flux LED blue [color=Blue]  # not connected
  LED2 = Super Flux LED blue [color=Blue]  # not connected
  LED3 = Super Flux LED blue [color=Blue]  # not connected
  LED4 = Super Flux LED blue [color=Blue]  # not connected
  LED5 = Super Flux LED blue [color=Blue]  # not connected
  LED6 = Super Flux LED blue [color=Blue]  # not connected
  LED7 = Super Flux LED blue [color=Blue]  # not connected
  LED8 = Super Flux LED blue [color=Blue]  # not connected
  LED9 = Super Flux LED blue [color=Blue]  # not connected
  LED10 = Super Flux LED blue [color=Blue]  # not connected
  LED12 = Super Flux LED blue [color=Blue]  # not connected
  LED13 = Super Flux LED blue [color=Blue]  # not connected
  LED14 = Super Flux LED blue [color=Blue]  # not connected
  LED15 = Super Flux LED blue [color=Blue]  # not connected
  LED16 = Super Flux LED blue [color=Blue]  # not connected
  LED17 = Super Flux LED blue [color=Blue]  # not connected
  LED18 = Super Flux LED blue [color=Blue]  # not connected
  LED19 = Super Flux LED blue [color=Blue]  # not connected
  LED20 = Super Flux LED blue [color=Blue]  # not connected
  LED21 = Super Flux LED blue [color=Blue]  # not connected
  LED22 = Super Flux LED blue [color=Blue]  # not connected
  LED23 = Super Flux LED blue [color=Blue]  # not connected
  LED24 = Super Flux LED blue [color=Blue]
  LED25 = Super Flux LED blue [color=Blue]
  LED26 = Super Flux LED blue [color=Blue]  # not connected
  J1 = female pin header, 15 pins [form="♀ (female)"]
  J2 = female pin header, 15 pins [form="♀ (female)"]
  S1 = Pushbutton [package="[THT]"]
  S2 = Pushbutton [package="[THT]"]
  R1 = Resistor [tolerance=±5% resistance=10k package=THT]
  R2 = Resistor [tolerance=±5% resistance=10k package=THT]
  J6 = female pin header, 6 pins [form="♀ (female)"]  # not connected
  부품1 = Arduino Nano (Rev3.0)

nets:
  N1: LED24.cathode, LED25.cathode
  N2: J1.pin1, 부품1.D13/SCK
  N3: J1.pin2, 부품1.3V3
  N4: J1.pin3, 부품1.AREF
  N5: J1.pin4, 부품1.A0
  N6: J1.pin5, 부품1.A1
  N7: J1.pin6, 부품1.A2
  N8: J1.pin7, 부품1.A3
  N9: J1.pin8, 부품1.A4
  N10: J1.pin9, 부품1.A5
  N11: J1.pin10, 부품1.A6
  N12: J1.pin11, 부품1.A7
  N13: J1.pin12, 부품1.5V
  N14: J1.pin13, J2.pin13, 부품1.RESET
  N15: J1.pin14, J2.pin12, 부품1.GND
  N16: J1.pin15, 부품1.VIN
  N17: J2.pin1, 부품1.D12/MISO
  N18: J2.pin2, 부품1.D11/MOSI
  N19: J2.pin3, 부품1.D10
  N20: J2.pin4, 부품1.D9
  N21: J2.pin5, 부품1.D8
  N22: J2.pin6, 부품1.D7
  N23: J2.pin7, 부품1.D6
  N24: J2.pin8, 부품1.D5
  N25: J2.pin9, 부품1.D4
  N26: J2.pin10, 부품1.D3
  N27: J2.pin11, 부품1.D2
  N28: J2.pin14, 부품1.D0/RX
  N29: J2.pin15, 부품1.D1/TX
  N30: S1.Pin_1, S1.Pin_2
  N31: S1.Pin_3, S1.Pin_4, R2.Pin_1
  N32: S2.Pin_1, S2.Pin_2
  N33: S2.Pin_3, S2.Pin_4, R1.Pin_1
