# Fritzing sketch 05servo (saved by Fritzing 0.9.3b)
breadboards: 1

parts:
  부품1 = Arduino Uno (Rev3)
  J1 = Basic Servo

nets:
  N1: 부품1.D9_PWM, J1.pulse
  5V: 부품1.5V, J1.vcc
  GND: 부품1.GND, J1.gnd
