# Fritzing sketch ch3_05_photogate (saved by Fritzing 0.9.3b)
breadboards: 1

parts:
  부품1 = Arduino Uno (Rev3)
  R1 = Photocell (LDR) [package=THT]
  R2 = Resistor [tolerance=±5% resistance=10k package=THT]
  LED1 = LED - 5mm [color="Red (633nm)" package="5 mm [THT]"]
  R3 = Resistor [tolerance=±5% resistance=220 package=THT]

nets:
  N1: 부품1.A0, R1.pin_1, R2.Pin_1
  N2: 부품1.5V, R1.pin_0, LED1.anode
  N3: 부품1.GND, R2.Pin_0, R3.Pin_0
  N4: LED1.cathode, R3.Pin_1
