# Fritzing sketch ch5_01_ultrasonic (saved by Fritzing 0.9.3b)
breadboards: 1

parts:
  부품1 = Arduino Uno (Rev3)
  hc-sr1 = hc-sr04

nets:
  N1: 부품1.D12/MISO, hc-sr1.Echo
  N2: 부품1.D13/SCK, hc-sr1.Trig
  5V: 부품1.5V, hc-sr1.VCC
  GND: 부품1.GND, hc-sr1.GND
