# Fritzing sketch ch5_06_radar (saved by Fritzing 0.9.3b)
breadboards: 1

parts:
  부품1 = Arduino Uno (Rev3)
  hc-sr1 = hc-sr04
  J1 = Basic Servo

nets:
  N1: 부품1.D12/MISO, hc-sr1.Echo
  N2: 부품1.D13/SCK, hc-sr1.Trig
  N3: 부품1.D6_PWM, J1.pulse
  VCC: 부품1.5V, hc-sr1.VCC, J1.vcc
  GND: 부품1.GND, hc-sr1.GND, J1.gnd
