# Fritzing sketch minicar_04_2motor_LED (saved by Fritzing 0.9.3b)
breadboards: 1

parts:
  부품1 = Arduino Nano (Rev3.0)
  Q1 = NPN-Transistor [package="TO92 [THT]"]
  R1 = Resistor [tolerance=±5% resistance=220 package=THT]
  Q2 = NPN-Transistor [package="TO92 [THT]"]
  R2 = Resistor [tolerance=±5% resistance=220 package=THT]
  M1 = DC Motor
  M2 = DC Motor
  LED1 = LED - 5mm [color="Red (633nm)" package="5 mm [THT]"]
  LED2 = LED - 5mm [color="Red (633nm)" package="5 mm [THT]"]
  R3 = Resistor [tolerance=±5% resistance=220 package=THT]
  R4 = Resistor [tolerance=±5% resistance=220 package=THT]

nets:
  N1: 부품1.GND, M1.pin_2, M2.pin_1, R3.Pin_0, R4.Pin_1
  N2: 부품1.D9, R1.Pin_1
  N3: 부품1.D10, R2.Pin_1
  N4: 부품1.D12/MISO, LED2.anode
  VIN: 부품1.VIN, 부품1.5V, Q1.C, Q2.C
  N5: 부품1.D13/SCK, LED1.anode
  N6: Q1.E, M1.pin_1
  N7: Q1.B, R1.Pin_0
  N8: Q2.E, M2.pin_2
  N9: Q2.B, R2.Pin_0
  N10: LED1.cathode, R4.Pin_0
  N11: LED2.cathode, R3.Pin_1
